# Fritzing sketch alarm_clock (saved by Fritzing 0.9.2b)
circuit board: 8.46667cm x 5.64444cm
breadboards: 1

parts:
  ATMEGA328 = atmega328 [package=dip]
  USB_Power = USB_MICROB_PLUG [package=micro-b-th]
  XTAL1 = Crystal [frequency="16 Mhz" package=THT]
  C1 = Electrolytic Capacitor [capacitance=100µF package="100 mil [THT, electrolytic]"]
  C2_22pF = Capacitor [package=cap-pth-small2]
  C3_22pF = Capacitor [package=cap-pth-small2]
  C1_100nF = Capacitor [package=cap-pth-small2]
  S1_Alarm = Toggle Switch [package=THT]
  LED1_Snooze = LEDs [package=led10mm]
  C4_1µF = Capacitor [package=cap-pth-small2]
  S0_RESET = SWITCH-MOMENTARY-2 [package=tactile-pth]
  Backup_Batt = Battery Holders [package=battcom_20mm_pth]
  Piezo = Piezo Speaker
  D1_Diode = Diode [package=diode-1n4148]
  S2_Snooze = SWITCH-MOMENTARY-2 [package=tactile-pth]
  R5 = TRIMPOT [package=trim_pot_pth]
  U1 = 7-SEGMENT-DISPLAY [package=7-segment-display]
  U2 = 7-SEGMENT-DISPLAY [package=7-segment-display]
  U3 = 7-SEGMENT-DISPLAY [package=7-segment-display]
  U4 = 7-SEGMENT-DISPLAY [package=7-segment-display]
  R1_?? = Resistor [tolerance=±5% resistance=220 package="1206 [SMD]"]
  R2 = Resistor [tolerance=±5% resistance=220 package="1206 [SMD]"]
  R3 = Resistor [tolerance=±5% resistance=220 package="1206 [SMD]"]
  DS3231_RTC = SO08 [chip_label=DS3231M package=SO]
  R4 = Resistor [tolerance=±5% resistance=1.5k package="1206 [SMD]"]
  U5 = 7-SEGMENT-4DIGIT-YOUNGSUN [package=7-segment-4digit-youngsun]  # not connected
  IC1 = IC, DIP package, 20 pins [chip_label=IC]
  LED2_Alarm = LED - 3mm [color="Green (570nm)" package="3 mm [THT]"]
  LED3_Dots2 = LED - 3mm [color="Orange (620nm)" package="3 mm [THT]"]
  LED3_Dots1 = LED - 3mm [color="Orange (620nm)" package="3 mm [THT]"]
  C4_1µF1 = Capacitor [package=cap-pth-small2]
  R6 = TRIMPOT [package=trim_pot_pth]
  R1_??2 = Resistor [tolerance=±5% resistance=220 package="1206 [SMD]"]
  R1_??1 = Resistor [tolerance=±5% resistance=220 package="1206 [SMD]"]
  R7 = Photocell (LDR) [package=THT]
  C2 = Electrolytic Capacitor [capacitance=330µF package="100 mil [THT, electrolytic]"]

nets:
  N1: ATMEGA328.RESET, S0_RESET.1
  N2: ATMEGA328.D3_(PWM), R4.Pin_1
  VCC: ATMEGA328.VCC, ATMEGA328.AVCC, USB_Power.VCC, C1.+, C1_100nF.1, R2.Pin_0, R3.Pin_0, DS3231_RTC.2, IC1.pin3, C4_1µF1.1
  GND: ATMEGA328.GND, USB_Power.GND, C1.-, C1_100nF.2, S1_Alarm.COM, LED1_Snooze.C, C4_1µF.2, S0_RESET.2, Backup_Batt.-, Piezo.pin1, D1_Diode.A, S2_Snooze.1, DS3231_RTC.5, IC1.pin14, C4_1µF1.2, R1_??1.Pin_1, R7.pin_0, C2.-
  N3: ATMEGA328.XLAT1, XTAL1.pin_1, C3_22pF.1
  N4: ATMEGA328.XLAT2, XTAL1.pin_0, C2_22pF.2
  N5: ATMEGA328.D5_(PWM), R1_??.Pin_0
  N6: ATMEGA328.D6_(PWM), IC1.pin10
  N7: ATMEGA328.D7, IC1.pin11
  N8: ATMEGA328.D8, IC1.pin12
  N9: ATMEGA328.A0, S1_Alarm.L2
  N10: ATMEGA328.A1, S1_Alarm.L1
  N11: ATMEGA328.A3, S2_Snooze.2
  N12: ATMEGA328.A4, R3.Pin_1, DS3231_RTC.8
  N13: ATMEGA328.A5, R2.Pin_1, DS3231_RTC.7
  N14: C2_22pF.1, C3_22pF.2
  N15: LED1_Snooze.A, R1_??.Pin_1
  N16: C4_1µF.1, Backup_Batt.+, DS3231_RTC.6
  N17: Piezo.pin2, D1_Diode.C, R5.CW
  N18: R5.WIPER, R4.Pin_0
  N19: U1.E, U2.E, U3.E, U4.E, IC1.pin2
  N20: U1.D, U2.D, U3.D, U4.D, IC1.pin4
  N21: U1.G1, IC1.pin16
  N22: U1.C, U2.C, U3.C, U4.C, IC1.pin5
  N23: U1.DP, U2.DP, U3.DP, U4.DP, IC1.pin19
  N24: U1.B, U2.B, U3.B, U4.B, IC1.pin6, LED2_Alarm.anode
  N25: U1.A, U2.A, U3.A, U4.A, IC1.pin7, LED3_Dots2.anode, LED3_Dots1.anode
  N26: U1.F, U2.F, U3.F, U4.F, IC1.pin1
  N27: U1.G, U2.G, U3.G
  N28: U2.G1, IC1.pin15
  N29: U3.G1, IC1.pin13
  N30: U4.G1, IC1.pin9
  N31: U4.G, IC1.pin20
  N32: IC1.pin8, R1_??2.Pin_0
  N33: IC1.pin17, LED2_Alarm.cathode, LED3_Dots2.cathode, LED3_Dots1.cathode
  N34: R6.WIPER, R1_??2.Pin_1, R7.pin_1, C2.+
  N35: R6.CW, R1_??1.Pin_0
